# Fritzing sketch esp32-cam-motion (saved by Fritzing 0.9.6b)
breadboards: 1

parts:
  ESP32_-_Back1 = ESP32 - CAM  # not connected
  Q1 = NPN-Transistor [package="TO92 [THT]"]
  R1 = Resistor [tolerance=±5% power=0.25 resistance=220 package=THT]
  R2 = Resistor [tolerance=±5% power=0.25 resistance=220 package=THT]

nets:
  N1: Q1.B, R1.Pin_0
  N2: Q1.C, R2.Pin_1

custom parts:
  ESP32 - CAM: The ESP32-CAM has a very competitive small-size camera module that can operate independently as a minimum system with a footprint of only 27*40.5*4.5mm and a deep sleep current of up to 6mA.
